# Fritzing sketch hardware_design (saved by Fritzing 0.9.2b)
perfboards: 1

parts:
  U1 = XBee
  RL = RELAY [package=relay-jzc]
  VCC1 = 4 x AAA Battery Mount
  R3 = Resistor [tolerance=±5% resistance=4.7k package=THT]
  U3 = Voltage Regulator - 3.3V [package="TO220 [THT]"]
  D1 = Rectifier Diode [part_number=1N4001 package="300 mil [THT]"]
  Q1 = NPN-Transistor [package="TO92 [THT]"]
  R2 = Resistor [tolerance=±5% resistance=33k package=THT]
  R1 = Resistor [tolerance=±5% resistance=1k package=THT]
  J1 = female pin header, 2 pins [form="♀ (female)"]

nets:
  N1: U1.VCC, U3.output_voltage
  N2: U1.pin6, R3.Pin_0, R1.Pin_0
  GND: U1.GND, VCC1.-, R3.Pin_1, U3.GND, Q1.E, R2.Pin_1
  N3: RL.COIL2, D1.anode, Q1.C
  N4: RL.NC, J1.pin1
  N5: RL.MAIN, J1.pin2
  N6: RL.COIL1, VCC1.+, U3.input_voltage, D1.cathode
  N7: Q1.B, R2.Pin_0, R1.Pin_1
